# Fritzing sketch doorlight pro mini (saved by Fritzing 0.9.2b)

parts:
  C1 = Electrolytic Capacitor [capacitance=100µF package="100 mil [THT, electrolytic]"]  # not connected
  R1 = Resistor [tolerance=±5% resistance=330 package=THT]  # not connected
  NEOPIXEL1 = Neopixel Strip -- White (30/m)
  proto2 = Adafruit_PermaProto_1_4_Board
  JACK1 = 2.1mm Barrel Jack with Terminal Block
  S1 = SWITCH-MOMENTARY-2 [package=reed_switch_pth]
  Part2 = Arduino Pro Mini v13

nets:
  N1: NEOPIXEL1.GND, proto2.connectorZ15
  N2: NEOPIXEL1.Din, proto2.connectorG15
  N3: NEOPIXEL1.+5V, proto2.connectorY15
  N4: proto2.connectorH10, Part2.D6_PWM
  N5: proto2.connectorY1, JACK1.POS
  N6: proto2.connectorY3, Part2.RAW
  N7: proto2.connectorZ1, JACK1.NEG
  N8: proto2.connectorZ2, Part2.GND
  N9: proto2.connectorZ7, S1.2
  N10: S1.1, Part2.D13/SCK

custom parts:
  Neopixel Strip -- White (30/m): These NeoPixel strips have 30 digitally-addressable pixel LEDs per meter and are very affordable and are only 12.5 mm wide, 10 mm if you remove the strip from the casing.
