# Fritzing sketch doorlight (saved by Fritzing 0.9.2b)

parts:
  Part1 = Arduino Uno (Rev3)
  C1 = Electrolytic Capacitor [capacitance=100µF package="100 mil [THT, electrolytic]"]  # not connected
  R1 = Resistor [tolerance=±5% resistance=220 package=THT]  # not connected
  NEOPIXEL1 = Neopixel Strip -- White (30/m)
  proto2 = Adafruit_PermaProto_1_4_Board
  JACK1 = 2.1mm Barrel Jack with Terminal Block
  S1 = SWITCH-MOMENTARY-2 [package=reed_switch_pth]

nets:
  N1: Part1.D13/SCK, S1.1
  N2: Part1.D6_PWM, proto2.connectorI11
  N3: Part1.GND, proto2.connectorZ2
  N4: NEOPIXEL1.GND, proto2.connectorZ15
  N5: NEOPIXEL1.Din, proto2.connectorG15
  N6: NEOPIXEL1.+5V, proto2.connectorY15
  N7: proto2.connectorY1, JACK1.POS
  N8: proto2.connectorZ1, JACK1.NEG
  N9: proto2.connectorZ5, S1.2

custom parts:
  Neopixel Strip -- White (30/m): These NeoPixel strips have 30 digitally-addressable pixel LEDs per meter and are very affordable and are only 12.5 mm wide, 10 mm if you remove the strip from the casing.
